// Logisim project project-pross.circ as structural Verilog
module main (
  input  [15:0] in_1,
  input  in_2,
  output BEQ,
  output BNQ,
  output SLL
);

  wire adder_2_cout, CU_alu_mux, CU_pc, CU_rimem, CU_writemem;
  wire [2:0] CU_op_code, CU_rig_write;
  wire [3:0] CU_sll, IR_q;
  wire [11:0] bit_extender_1_out;
  wire [15:0] adder_1_out, ALU_out_5, bit_extender_2_out, bit_extender_3_out, multiplexer_1_out,
       multiplexer_2_out, PC_q, ram_1_data, RF_r1, RF_r2, undriven;

  Register #(.width(16)) PC (.D(multiplexer_1_out), .Q(PC_q), .clk(in_2));  // open: en, clr
  Multiplexer #(.select(2), .width(16)) multiplexer_1 (
    .in0(adder_1_out), .in1(adder_1_out), .in2(undriven), .out(multiplexer_1_out), .en(CU_pc));  // open: in3, sel
  Adder #(.width(16)) adder_1 (.b(bit_extender_2_out), .out(adder_1_out));  // open: a, cin, cout
  Adder #(.width(16)) adder_2 (.a(in_1), .b(PC_q), .out(adder_1_out), .cin(1'b0), .cout(adder_2_cout));
  Bit_Extender #(.in_width(16), .out_width(12)) bit_extender_1 (.in(undriven), .out(bit_extender_1_out));
  RAM #(.addrWidth(16), .dataWidth(16)) ram_1 (
    .addr(PC_q), .data(ram_1_data), .sel(CU_rimem), .clk(in_2));  // open: ld, clr
  Register #(.width(16)) IR (.D(ram_1_data), .Q({bit_extender_1_out, IR_q}), .clk(in_2));  // open: en, clr
  assign bit_extender_2_out = {{10{1'b0}}, bit_extender_1_out[11:6]};  // Bit_Extender bit_extender_2
  Control_unit CU (
    .op0(IR_q[0]), .op1(IR_q[1]), .op2(IR_q[2]), .op3(IR_q[3]), .PC(CU_pc), .Rig_Write(CU_rig_write),
    .ALU_MUX(CU_alu_mux), .WriteMem(CU_writemem), .RiMem(CU_rimem), .op_code(CU_op_code), .SLL(CU_sll));
  assign bit_extender_3_out = {{7{1'b0}}, bit_extender_1_out[11:3]};  // Bit_Extender bit_extender_3
  Multiplexer #(.select(2), .width(16)) multiplexer_2 (
    .in0(RF_r2), .in1(bit_extender_3_out), .in2(ALU_out_5), .out(multiplexer_2_out), .en(CU_alu_mux));  // open: in3, sel
  RF RF (
    .Data(multiplexer_2_out), .en_Write(CU_rig_write), .sel_R1(bit_extender_1_out[2:0]),
    .sel_R2(bit_extender_1_out[5:3]), .R1(RF_r1), .R2(RF_r2));
  ALU_16bits ALU (
    .R1(RF_r1), .R2(RF_r2), .shift_left_cont(CU_sll), .MUX__OPcode(CU_op_code), .out_5(ALU_out_5),
    .carry_out(SLL), .BNQ(BNQ), .BEQ(BEQ));
  RAM #(.addrWidth(16), .dataWidth(16)) ram_2 (.addr(RF_r1), .data(RF_r2), .sel(CU_writemem));  // open: clk, ld, clr
  // also tied to GND on the sheet: adder_2_cout
endmodule

module full_adder_1bit (
  input  a,
  input  b,
  input  z,
  output out,
  output co
);

  wire and_1_out, and_2_out, and_3_out, and_4_out, and_5_out, and_6_out, and_7_out, not_1_out, not_2_out,
       not_3_out;

  not not_1 (not_1_out, a);
  not not_2 (not_2_out, b);
  not not_3 (not_3_out, z);
  and and_1 (and_1_out, not_1_out, not_2_out, z);
  and and_2 (and_2_out, not_1_out, b, not_3_out);
  and and_3 (and_3_out, a, not_2_out, not_3_out);
  and and_4 (and_4_out, a, b, z);
  and and_5 (and_5_out, a, b);
  and and_6 (and_6_out, a, z);
  and and_7 (and_7_out, b, z);
  or or_1 (out, and_1_out, and_2_out, and_3_out, and_4_out);
  or or_2 (co, and_5_out, and_6_out, and_7_out);
endmodule

module ALU__1bit (
  input  BMux,
  input  A,
  input  B,
  input  in_4,
  input  in_5,
  input  [2:0] Mux_con,
  output carry_out,
  output Output
);

  wire and_1_out, full_adder_1bit_1_out, multiplexer_1_out, multiplexer_2_out, nand_1_out, not_1_out,
       or_1_out;

  Multiplexer multiplexer_1 (.in0(1'b0), .in1(1'b1), .out(multiplexer_1_out), .sel(BMux), .en(1'b1));
  not not_1 (not_1_out, B);
  Multiplexer multiplexer_2 (.in0(B), .in1(not_1_out), .out(multiplexer_2_out), .sel(BMux), .en(1'b1));
  full_adder_1bit full_adder_1bit_1 (
    .a(A), .b(multiplexer_2_out), .z(multiplexer_1_out), .out(full_adder_1bit_1_out), .co(carry_out));
  and and_1 (and_1_out, A, B);
  or or_1 (or_1_out, A, B);
  nand nand_1 (nand_1_out, A, B);
  Multiplexer #(.select(3)) multiplexer_3 (
    .in0(full_adder_1bit_1_out), .in1(and_1_out), .in2(or_1_out), .in3(nand_1_out), .in4(in_4), .in5(in_5),
    .in6(1'b0), .in7(1'b0), .out(Output), .sel(Mux_con), .en(1'b1));
endmodule

module ALU_16bits (
  input  [15:0] R1,
  input  [15:0] R2,
  input  [3:0] shift_left_cont,
  input  [2:0] MUX__OPcode,
  output [15:0] out_5,
  output carry_out,
  output BNQ,
  output BEQ
);

  wire adder_1_cout, subtractor_1_bout;
  wire [15:0] adder_1_out, nand_1_out, nor_1_out, shifter_1_out, shifter_2_out, subtractor_1_out;

  Adder #(.width(16)) adder_1 (.a(R1), .b(R2), .out(adder_1_out), .cin(1'b0), .cout(adder_1_cout));
  Subtractor #(.width(16)) subtractor_1 (.a(R1), .b(R2), .out(subtractor_1_out), .bin(1'b0), .bout(subtractor_1_bout));
  Shifter #(.width(16)) shifter_1 (.in(R1), .\dist (shift_left_cont), .out(shifter_1_out));
  Shifter #(.width(16), .shift("lr")) shifter_2 (.in(R1), .\dist (shift_left_cont), .out(shifter_2_out));
  assign nand_1_out = ~(R1 & R2);  // NAND_Gate nand_1, 16 bits wide
  assign nor_1_out = ~(R1 | R2);  // NOR_Gate nor_1, 16 bits wide
  Comparator #(.width(16)) comparator_1 (.a(R1), .b(R2), .eq(BEQ));  // open: gt, lt
  Multiplexer #(.select(3), .width(16)) multiplexer_1 (
    .in0(adder_1_out), .in1(subtractor_1_out), .in2(shifter_1_out), .in3(shifter_2_out), .in4(nand_1_out),
    .in5(nor_1_out), .out(out_5), .sel(MUX__OPcode));  // open: in6, in7, en
  or or_1 (carry_out, adder_1_cout, subtractor_1_bout);
  not not_1 (BNQ, BEQ);
endmodule

module reg_8bits_flip (
  input  clock,
  input  [15:0] data,
  output [15:0] out
);

  D_Flip_Flop d_ff_1 (.clk(clock), .D(data[15]), .Q(out[15]), .en(1'b1));  // open: Qn, preset, reset
  D_Flip_Flop d_ff_2 (.clk(clock), .D(data[1]), .Q(out[1]), .en(1'b1));  // open: Qn, preset, reset
  D_Flip_Flop d_ff_3 (.clk(clock), .D(data[2]), .Q(out[2]), .en(1'b1));  // open: Qn, preset, reset
  D_Flip_Flop d_ff_4 (.clk(clock), .D(data[3]), .Q(out[3]), .en(1'b1));  // open: Qn, preset, reset
  D_Flip_Flop d_ff_5 (.clk(clock), .D(data[4]), .Q(out[4]), .en(1'b1));  // open: Qn, preset, reset
  D_Flip_Flop d_ff_6 (.clk(clock), .D(data[5]), .Q(out[5]), .en(1'b1));  // open: Qn, preset, reset
  D_Flip_Flop d_ff_7 (.clk(clock), .D(data[6]), .Q(out[6]), .en(1'b1));  // open: Qn, preset, reset
  D_Flip_Flop d_ff_8 (.clk(clock), .D(data[7]), .Q(out[7]), .en(1'b1));  // open: Qn, preset, reset
  D_Flip_Flop d_ff_9 (.clk(clock), .D(data[8]), .Q(out[8]), .en(1'b1));  // open: Qn, preset, reset
  D_Flip_Flop d_ff_10 (.clk(clock), .D(data[9]), .Q(out[9]), .en(1'b1));  // open: Qn, preset, reset
  D_Flip_Flop d_ff_11 (.clk(clock), .D(data[10]), .Q(out[10]), .en(1'b1));  // open: Qn, preset, reset
  D_Flip_Flop d_ff_12 (.clk(clock), .D(data[11]), .Q(out[11]), .en(1'b1));  // open: Qn, preset, reset
  D_Flip_Flop d_ff_13 (.clk(clock), .D(data[12]), .Q(out[12]), .en(1'b1));  // open: Qn, preset, reset
  D_Flip_Flop d_ff_14 (.clk(clock), .D(data[13]), .Q(out[13]), .en(1'b1));  // open: Qn, preset, reset
  D_Flip_Flop d_ff_15 (.clk(clock), .D(data[14]), .Q(out[14]), .en(1'b1));  // open: Qn, preset, reset
  D_Flip_Flop d_ff_16 (.clk(clock), .D(data[0]), .Q(out[0]), .en(1'b1));  // open: Qn, preset, reset
endmodule

module RF (
  input  [15:0] Data,
  input  [2:0] sel_R1,
  input  [2:0] en_Write,
  input  [2:0] sel_R2,
  output [15:0] R1,
  output [15:0] R2
);

  wire decoder_1_out0, decoder_1_out1, decoder_1_out2, decoder_1_out3, decoder_1_out4, decoder_1_out5,
       decoder_1_out6, decoder_1_out7;
  wire [15:0] reg_8bits_flip_1_out, reg_8bits_flip_2_out, reg_8bits_flip_3_out, reg_8bits_flip_4_out,
       reg_8bits_flip_5_out, reg_8bits_flip_6_out, reg_8bits_flip_7_out, reg_8bits_flip_8_out;

  Decoder #(.select(3)) decoder_1 (
    .out0(decoder_1_out0), .out1(decoder_1_out1), .out2(decoder_1_out2), .out3(decoder_1_out3),
    .out4(decoder_1_out4), .out5(decoder_1_out5), .out6(decoder_1_out6), .out7(decoder_1_out7), .sel(en_Write));  // open: en
  reg_8bits_flip reg_8bits_flip_1 (.data(Data), .clock(decoder_1_out0), .out(reg_8bits_flip_1_out));
  reg_8bits_flip reg_8bits_flip_2 (.data(Data), .clock(decoder_1_out1), .out(reg_8bits_flip_2_out));
  reg_8bits_flip reg_8bits_flip_3 (.data(Data), .clock(decoder_1_out2), .out(reg_8bits_flip_3_out));
  reg_8bits_flip reg_8bits_flip_4 (.data(Data), .clock(decoder_1_out3), .out(reg_8bits_flip_4_out));
  reg_8bits_flip reg_8bits_flip_5 (.data(Data), .clock(decoder_1_out4), .out(reg_8bits_flip_5_out));
  reg_8bits_flip reg_8bits_flip_6 (.data(Data), .clock(decoder_1_out5), .out(reg_8bits_flip_6_out));
  reg_8bits_flip reg_8bits_flip_7 (.data(Data), .clock(decoder_1_out6), .out(reg_8bits_flip_7_out));
  reg_8bits_flip reg_8bits_flip_8 (.data(Data), .clock(decoder_1_out7), .out(reg_8bits_flip_8_out));
  Multiplexer #(.select(3), .width(16)) multiplexer_1 (
    .in0(reg_8bits_flip_1_out), .in1(reg_8bits_flip_2_out), .in2(reg_8bits_flip_3_out),
    .in3(reg_8bits_flip_4_out), .in4(reg_8bits_flip_5_out), .in5(reg_8bits_flip_6_out),
    .in6(reg_8bits_flip_7_out), .in7(reg_8bits_flip_8_out), .out(R1), .sel(sel_R1));  // open: en
  Multiplexer #(.select(3), .width(16)) multiplexer_2 (
    .in0(reg_8bits_flip_1_out), .in1(reg_8bits_flip_2_out), .in2(reg_8bits_flip_3_out),
    .in3(reg_8bits_flip_4_out), .in4(reg_8bits_flip_5_out), .in5(reg_8bits_flip_6_out),
    .in6(reg_8bits_flip_7_out), .in7(reg_8bits_flip_8_out), .out(R2), .sel(sel_R2));  // open: en
endmodule

module Control_unit (
  input  op0,
  input  op1,
  input  op2,
  input  op3,
  output PC,
  output [2:0] Rig_Write,
  output ALU_MUX,
  output WriteMem,
  output RiMem,
  output [2:0] op_code,
  output [3:0] SLL
);

  wire and_1_out, I_bransh_out, I_out, J_out, or_2_out, R_out;

  and R (R_out, op0, op1, op2, op3);
  and I (I_out, op0, op1, op2, op3);
  and I_bransh (I_bransh_out, op0, op1, op2, op3);
  and I_read (RiMem, op0, op1, op2, op3);
  and I_Write (WriteMem, op0, op1, op2, op3);
  and J (J_out, op0, op1, op2, op3);
  and and_1 (and_1_out, op0, op1, op2, op3);
  assign SLL = {{3{1'b0}}, and_1_out};  // Bit_Extender bit_extender_1
  or or_1 (PC, I_bransh_out, J_out);
  or or_2 (or_2_out, R_out, I_out, WriteMem, RiMem);
  or or_3 (ALU_MUX, I_bransh_out, RiMem, WriteMem);
  assign Rig_Write = {{2{1'b0}}, or_2_out};  // Bit_Extender bit_extender_2

  assign op_code = {op2, op1, op0};
endmodule
